// Logisim project display.circ as structural Verilog: 1 circuit, main circuit main
module main (
);

  wire clock_1_out, nor_1_out, reset_out;
  wire [7:0] counter_1_q, rom_1_data, shift_register_1_p8;

  Clock clock_1 (.out(clock_1_out));
  ROM rom_1 (.addr(counter_1_q), .data(rom_1_data));
  Button reset (.out(reset_out));
  Counter counter_1 (
    .clr(reset_out), .load(1'b0), .up(1'b1), .count(1'b1), .clk(clock_1_out), .Q(counter_1_q));  // open: D, carry
  nor nor_1 (nor_1_out, counter_1_q[0], counter_1_q[1], counter_1_q[2]);
  // Shift_Register #(.trigger("falling")) shift_register_1: pin names not known; wires that end beside it: nor_1_out, 1'b1, reset_out, 1'b0, 1'b1, clock_1_out, nor_1_out, shift_register_1_p8[0], shift_register_1_p8[1], shift_register_1_p8[2]
  // DotMatrix #(.inputtype("select"), .matrixcols(8), .matrixrows(8), .persist(32)) dotmatrix_1: pin names not known; wires that end beside it: rom_1_data, shift_register_1_p8, shift_register_1_p8[3], shift_register_1_p8[4], shift_register_1_p8[5], shift_register_1_p8[6], shift_register_1_p8[7]
  // Shift_Register #(.width(8)) shift_register_2: pin names not known

  // Notes on the sheet:
  //   contents of rom_1 (hex, n*v repeats v):
  //   3c 66 3 3 73 66 7c 0 0 0 1e 30 3e 33 6e 0 0 0 6e 33 33 3e 30 1f 0 0 1e 30 3e 33 6e 0 0 0 1f 4*33 9*0
  //   67 66 36 1e 36 66 67 0 0 0 4*33 6e 0 0 0 33 7f 7f 6b 63 0 0 0 1e 30 3e 33 6e 0 0 0 3b 6e 66 6 f
endmodule
